# Fritzing sketch vinification-controller (saved by Fritzing 0.9.3b)
circuit board: 5cm x 5cm

parts:
  Q1_cooling_mosfet = MOSFET-NCHANNEL [package=to220v]
  Q2_heating_mosfet = MOSFET-NCHANNEL [package=to220v]
  J9_-_heating_connector = screw terminal, 2 pins
  J9_-_cooling_connector = screw terminal, 2 pins
  U1_3_3V_regulator = Voltage Regulator - 3.3V [package="TO220 [THT]"]
  Part1 = ESP-WROOM-32 [ESP-32S] Module [part_number=ESP-WROOM-32]
  J9_-_tankThermometer = screw terminal, 3 pins
  J9_-_ambientThermometer = screw terminal, 3 pins
  R1 = Resistor [tolerance=±5% resistance=4.7k package=THT]
  J9_-_power_connector = screw terminal, 2 pins
  J1 = female pin header, 4 pins [form="♀ (female)"]

nets:
  N1: Q1_cooling_mosfet.G, Part1.IO23
  N2: Q1_cooling_mosfet.D, J9_-_cooling_connector.pin1
  N3: Q1_cooling_mosfet.S, Q2_heating_mosfet.S, J9_-_power_connector.pin2
  N4: Q2_heating_mosfet.G, Part1.IO22
  N5: Q2_heating_mosfet.D, J9_-_heating_connector.pin1
  GND: J9_-_heating_connector.pin2, J9_-_cooling_connector.pin2, U1_3_3V_regulator.GND, Part1.GND, J9_-_tankThermometer.pin3, J9_-_ambientThermometer.pin3, J9_-_power_connector.pin1, J1.pin2
  N6: U1_3_3V_regulator.input_voltage, J9_-_tankThermometer.pin1, J9_-_ambientThermometer.pin1, R1.Pin_0
  N7: U1_3_3V_regulator.output_voltage, Part1.3V3, J1.pin1
  N8: Part1.IO21, J9_-_tankThermometer.pin2, J9_-_ambientThermometer.pin2, R1.Pin_1
  N9: Part1.RXD0, J1.pin3
  N10: Part1.TXD0, J1.pin4

custom parts:
  ESP-WROOM-32 [ESP-32S] Module: Espressif ESP-WROOM-32 WiFi/Bluetooth LE microcontroller module also known as the Ai-Thinker ESP-32S module with similar formfactor. The ESP32 is a microcontroller chip with WiFi and BLE capabilities. The chip is developed by Espressif and is the successor to the popular ESP8266 WiFi module.
